# Fritzing sketch no-pcb (saved by Fritzing 0.9.3b)

parts:
  Battery = Battery block 9V
  Pusher_Motor = DC Motor
  R1 = Resistor [tolerance=±5% resistance=4.7 package="0805 [SMD]"]
  CPU = Arduino Nano (Rev3.0)
  Flywheel_Switch = Taiway 100-SP-X-T1 SPDT Miniature Toggle Switch [part_number=100-SP-X-T1-0-0-B1-M1 package=THT]
  Trigger_Switch = Taiway 100-SP-X-T1 SPDT Miniature Toggle Switch [part_number=100-SP-X-T1-0-0-B1-M1 package=THT]
  Disconnector_Switch = Taiway 100-SP-X-T1 SPDT Miniature Toggle Switch [part_number=100-SP-X-T1-0-0-B1-M1 package=THT]
  Cycle_Switch = Taiway 100-SP-X-T1 SPDT Miniature Toggle Switch [part_number=100-SP-X-T1-0-0-B1-M1 package=THT]
  Auto_Switch = Taiway 100-SP-X-T1 SPDT Miniature Toggle Switch [part_number=100-SP-X-T1-0-0-B1-M1 package=THT]
  100k2 = Resistor [tolerance=±5% resistance=100k package=THT]
  1M2 = Resistor [tolerance=±5% resistance=1M package=THT]

nets:
  N1: Battery.-, Pusher_Motor.pin_2, R1.Pin_1, CPU.GND, 100k2.Pin_1
  N2: Battery.+, CPU.VIN, Trigger_Switch.COM, Cycle_Switch.COM, 1M2.Pin_0
  N3: Pusher_Motor.pin_1, Cycle_Switch.L2, Auto_Switch.L2
  N4: R1.Pin_0, CPU.D3, Flywheel_Switch.L2
  N5: CPU.5V, Flywheel_Switch.COM
  N6: CPU.A0, 100k2.Pin_0, 1M2.Pin_1
  N7: Trigger_Switch.L2, Disconnector_Switch.COM
  N8: Disconnector_Switch.L2, Auto_Switch.COM
