# Fritzing sketch pcb-v2 (saved by Fritzing 0.9.3b)
circuit board: 7.7cm x 3.8cm
perfboards: 1

parts:
  Motor_IC = L293D [package=THT]
  4_7k = Resistor [tolerance=±5% resistance=4.7 package=THT]
  Stepper = female pin header, 4 pins [form="♀ (female)"]
  1M = Resistor [tolerance=±5% resistance=1M package=THT]
  100k = Resistor [tolerance=±5% resistance=100k package=THT]
  4_7k_2 = Resistor [tolerance=±5% resistance=4.7 package=THT]
  4_7k_3 = Resistor [tolerance=±5% resistance=4.7 package=THT]
  OLED = female pin header, 4 pins [form="♀ (female)"]
  Pot = female pin header, 3 pins [form="♀ (female)"]
  11v-Out = female pin header, 2 pins [form="♀ (female)"]
  BAT = female pin header, 2 pins [form="♀ (female)"]
  Step-Pow = female pin header, 2 pins [form="♀ (female)"]
  Arduino_Nano = Arduino Nano (Rev3.0)
  ESC_Lower = female pin header, 3 pins [form="♀ (female)"]
  ESC_Upper = female pin header, 3 pins [form="♀ (female)"]
  Display = female pin header, 2 pins [form="♀ (female)"]
  Reload = female pin header, 2 pins [form="♀ (female)"]
  Tigger = female pin header, 2 pins [form="♀ (female)"]

nets:
  N1: Motor_IC.Enable_1, Motor_IC.Enable_2, Motor_IC.+V, OLED.pin2, Pot.pin2, Arduino_Nano.5V, Display.pin1, Reload.pin1, Tigger.pin1
  N2: Motor_IC.In_1, Arduino_Nano.D3
  N3: Motor_IC.Out_1_(_Controlled_by_Enable_1_), Stepper.pin1
  N4: Motor_IC.0V, 4_7k.Pin_1, 100k.Pin_1, 4_7k_2.Pin_1, 4_7k_3.Pin_1, OLED.pin1, Pot.pin1, 11v-Out.pin2, BAT.pin2, Step-Pow.pin1, Arduino_Nano.GND
  N5: Motor_IC.Out_2_(_Controlled_by_Enable_1_), Stepper.pin2
  N6: Motor_IC.In_2, Arduino_Nano.D4
  N7: Motor_IC.+Vmotor, Step-Pow.pin2
  N8: Motor_IC.In_3, Arduino_Nano.D5
  N9: Motor_IC.Out_3_(_Controlled_by_Enable_2_), Stepper.pin3
  N10: Motor_IC.Out_4_(_Controlled_by_Enable_2_), Stepper.pin4
  N11: Motor_IC.In_4, Arduino_Nano.D6
  N12: 4_7k.Pin_0, Arduino_Nano.D11/MOSI, Tigger.pin2
  N13: 1M.Pin_0, 100k.Pin_0, Arduino_Nano.A2
  N14: 1M.Pin_1, 11v-Out.pin1, BAT.pin1, Arduino_Nano.VIN
  N15: 4_7k_2.Pin_0, Arduino_Nano.D10, Reload.pin2
  N16: 4_7k_3.Pin_0, Arduino_Nano.D9, Display.pin2
  N17: OLED.pin3, Arduino_Nano.A5
  N18: OLED.pin4, Arduino_Nano.A4
  N19: Pot.pin3, Arduino_Nano.A3
  N20: Arduino_Nano.D7, ESC_Lower.pin1
  N21: Arduino_Nano.D8, ESC_Upper.pin1
